# Fritzing sketch sketch (saved by Fritzing 1.0.5)
breadboards: 1

parts:
  S1 = 0.91 inch OLED I2C Display 128 x 32 Pixels
  Part1 = Adafruit BMP280 [part_number="Adafruit #2651"]
  U1 = ESP32-38PinWide [part_number=ESP32-38PinWide]

nets:
  VCC: S1.VCC, Part1.VCC, U1.3.3
  GND: S1.GND, S1.SCL, Part1.SCK/SCL, Part1.GND, U1.GND, U1.GPIO22
  N1: S1.SDA, Part1.SDI/SDA, U1.GPIO21

custom parts:
  Adafruit BMP280: Bosch has stepped up their game with their new BMP280 sensor, an environmental sensor with temperature, barometric pressure that is the next generation upgrade to the BMP085/BMP180/BMP183. This sensor is great for all sorts of weather sensing and can even be used in both I2C and SPI! This precision sensor from Bosch is the best low-cost, precision sensing solution for measuring barometric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
  ESP32-38PinWide: Generic 38-Pin ESP32 with wide format (only access to one side of pins on a breadboard) based on Stephen Lilley's HiLetgo ESP-WROOM-32 ESP32 ESP-32S Development Board.
